# Fritzing sketch Sensor_side (saved by Fritzing 0.9.10b)
breadboards: 2

parts:
  부품1 = Arduino Uno (Rev3)
  부품2 = HY-SRF05 Ultrasonic Rangefinder
  LCD2 = LCD screen
  LCM1602_IIC2 = LCM1602 IIC [part_number="LCM1602 IIC" chip_label="LCM1602 IIC" package="DIP (Dual Inline) [THT]"]
  A1 = BBAA100043
  LED1 = smd LED [color="Red (633nm)" package="1206 [SMD]"]
  J1 = Piezo Speaker

nets:
  N1: 부품1.A4/SDA, LCM1602_IIC2.SDA
  N2: 부품1.A5/SCL, LCM1602_IIC2.SCL
  N3: 부품1.D8, J1.pin1
  N4: 부품1.D12/MISO, 부품2.Echo
  N5: 부품1.D13/SCK, 부품2.Trig
  N6: 부품1.D5_PWM, A1.pin3, LED1.anode
  N7: 부품1.D6_PWM, A1.pin2
  N8: 부품1.D7, A1.pin1
  VCC: 부품1.5V, 부품2.Vcc, LCM1602_IIC2.VCC, J1.pin2
  GND: 부품1.GND, 부품2.GND, LCM1602_IIC2.GND, A1.pin4, LED1.cathode
  VSS: LCD2.VSS, LCM1602_IIC2.VSS
  VDD: LCD2.VDD, LCM1602_IIC2.VDD
  N9: LCD2.V0, LCM1602_IIC2.V0
  N10: LCD2.RS, LCM1602_IIC2.RS
  N11: LCD2.R/W, LCM1602_IIC2.RW
  N12: LCD2.E, LCM1602_IIC2.E
  N13: LCD2.DB0, LCM1602_IIC2.D0
  N14: LCD2.DB1, LCM1602_IIC2.D1
  N15: LCD2.DB2, LCM1602_IIC2.D2
  N16: LCD2.DB3, LCM1602_IIC2.D3
  N17: LCD2.DB4, LCM1602_IIC2.D4
  N18: LCD2.DB5, LCM1602_IIC2.D5
  N19: LCD2.DB6, LCM1602_IIC2.D6
  N20: LCD2.DB7, LCM1602_IIC2.D7
  N21: LCD2.LED+, LCM1602_IIC2.A
  N22: LCD2.LED-, LCM1602_IIC2.K

custom parts:
  LCM1602 IIC: I2C-Module to use a 1602 or 2004 LCD on with the wire.h libory Serial LCD Modul
  BBAA100043: BBAA100043 traffic light module.
