# Fritzing sketch Server_side (saved by Fritzing 0.9.10b)
breadboards: 1

parts:
  A1 = WeMos D1 R1
  Part1 = KY-015 Temperature & Humidity Sensor Module [package="Breakout board"]
  R1 = PHOTOCELL [package=photocell-kit]
  R2 = Resistor [tolerance=±5% resistance=220 package="2010 [SMD]"]

nets:
  N1: A1.Pin_9, Part1.-, R1.P$2
  N2: A1.Pin_11, A1.Pin_13, Part1.S, R2.Pin_0
  N3: A1.Pin_17, R1.P$1, R2.Pin_1
  N4: A1.Pin_56, A1.Pin_60, Part1.Vin

custom parts:
  WeMos D1 R1: The WeMos D1 is a ESP8266 WiFi based board that uses the Arduino layout with a operating voltage of 3.3V.
  KY-015 Temperature & Humidity Sensor Module: KY-015 temperature and humidity sensor module, provides a low-latency serial interface to measure humidity and temperature.
